# Fritzing sketch Schematic (saved by Fritzing 0.9.3b)
breadboards: 1

parts:
  Driver2 = 28BYJ-48 Driver Module [part_number=ULN2003 package=THT]
  SM2 = 28BYJ-48 Stepper Motor [part_number=28BYJ-48]
  LCD2 = LCD screen
  LCM1602_IIC2 = LCM1602 IIC [part_number="LCM1602 IIC" chip_label="LCM1602 IIC" package="DIP (Dual Inline) [THT]"]
  Tiny_RTC2 = Tiny RTC  # not connected
  J1 = Piezo Speaker  # not connected
  S1 = Pushbutton [package="[SMD]"]  # not connected
  S2 = Pushbutton [package="[SMD]"]  # not connected
  S3 = Pushbutton [package="[SMD]"]  # not connected
  Componente1 = Arduino Mega 2560 (Rev3)  # not connected
  U2 = RELAY [package=relay-g5q]  # not connected
  M1 = RioRand LM2596  # not connected

nets:
  N1: Driver2.blue-pin, SM2.blue-pin
  N2: Driver2.pink-pin, SM2.pink-pin
  N3: Driver2.yellow-pin, SM2.yellow-pin
  N4: Driver2.orange-pin, SM2.orange-pin
  N5: Driver2.red-pin, SM2.red-pin
  VSS: LCD2.VSS, LCM1602_IIC2.VSS
  VDD: LCD2.VDD, LCM1602_IIC2.VDD
  N6: LCD2.V0, LCM1602_IIC2.V0
  N7: LCD2.RS, LCM1602_IIC2.RS
  N8: LCD2.R/W, LCM1602_IIC2.RW
  N9: LCD2.E, LCM1602_IIC2.E
  N10: LCD2.DB0, LCM1602_IIC2.D0
  N11: LCD2.DB1, LCM1602_IIC2.D1
  N12: LCD2.DB2, LCM1602_IIC2.D2
  N13: LCD2.DB3, LCM1602_IIC2.D3
  N14: LCD2.DB4, LCM1602_IIC2.D4
  N15: LCD2.DB5, LCM1602_IIC2.D5
  N16: LCD2.DB6, LCM1602_IIC2.D6
  N17: LCD2.DB7, LCM1602_IIC2.D7
  N18: LCD2.LED+, LCM1602_IIC2.A
  N19: LCD2.LED-, LCM1602_IIC2.K
  N20: LCM1602_IIC2.LED_A, LCM1602_IIC2.LED_B

custom parts:
  28BYJ-48 Driver Module: Generic male header
  28BYJ-48 Stepper Motor: Unipolar Stepper Motor 28BYJ-48 Top coil - pink & orange Bottom coil - blue & yellow Common rail - red Connector pins: blue - pink - yellow - orange - red
  LCM1602 IIC: I2C-Module to use a 1602 or 2004 LCD on with the wire.h libory Serial LCD Modul
  Tiny RTC: Tiny RTC I2C module DS1370Z RTC and AT24C32 EEPROM
